// Logisim project Oblig1.circ as structural Verilog: 8 circuits, main circuit main
module main (
  input  X2,
  input  X1,
  input  X0
);

  wire a_1_a, b_1_b, c_1_c, d_1_d, e_1_e, f_1_f, g_1_g;

  A a_1 (.X2(X2), .X1(X1), .X0(X0), .A(a_1_a));
  B b_1 (.X2(X2), .X1(X1), .X0(X0), .B(b_1_b));
  C c_1 (.X2(X2), .X1(X1), .X0(X0), .C(c_1_c));
  D d_1 (.X2(X2), .X1(X1), .X0(X0), .D(d_1_d));
  E e_1 (.X2(X2), .X1(X1), .X0(X0), .E(e_1_e));
  F f_1 (.X2(X2), .X1(X1), .X0(X0), .F(f_1_f));
  G g_1 (.X2(X2), .X1(X1), .X0(X0), .G(g_1_g));
  _7_Segment_Display u_7_segment_display_1 (
    .g(g_1_g), .f(f_1_f), .a(a_1_a), .b(b_1_b), .e(e_1_e), .d(d_1_d), .c(c_1_c));  // open: dp
endmodule

module A (
  input  X2,
  input  X1,
  input  X0,
  output A
);

  wire and_1_out, and_2_out, and_3_out, not_1_out, not_3_out;

  not not_1 (not_1_out, X2);
  // NOT_Gate not_2 has open pins: in=X1, out=open
  not not_3 (not_3_out, X0);
  and and_1 (and_1_out, X2, X0);
  and and_2 (and_2_out, X1, X0);
  and and_3 (and_3_out, not_1_out, not_3_out);
  or or_1 (A, and_1_out, and_2_out, and_3_out);
endmodule

module B (
  input  X2,
  input  X1,
  input  X0,
  output B
);

  wire and_1_out, not_1_out, not_2_out, not_3_out;

  not not_1 (not_1_out, X2);
  not not_2 (not_2_out, X1);
  not not_3 (not_3_out, X0);
  and and_1 (and_1_out, not_2_out, not_3_out);
  or or_1 (B, not_1_out, and_1_out);
endmodule

module C (
  input  X2,
  input  X1,
  input  X0,
  output C
);

  wire not_2_out;

  // NOT_Gate not_1 has open pins: in=X2, out=open
  not not_2 (not_2_out, X1);
  // NOT_Gate not_3 has open pins: in=X0, out=open
  or or_1 (C, X2, not_2_out, X0);
endmodule

module D (
  input  X2,
  input  X1,
  input  X0,
  output D
);

  wire and_1_out, and_2_out, and_3_out, and_4_out, not_1_out, not_2_out, not_3_out;

  not not_1 (not_1_out, X2);
  not not_2 (not_2_out, X1);
  not not_3 (not_3_out, X0);
  and and_1 (and_1_out, not_1_out, not_3_out, not_2_out);
  and and_2 (and_2_out, X2, X0, not_2_out);
  and and_3 (and_3_out, not_1_out, X1);
  and and_4 (and_4_out, X1, not_3_out);
  or or_1 (D, and_1_out, and_2_out, and_3_out, and_4_out);
endmodule

module E (
  input  X2,
  input  X1,
  input  X0,
  output E
);

  wire and_1_out, and_2_out, not_1_out, not_3_out;

  not not_1 (not_1_out, X2);
  // NOT_Gate not_2 has open pins: in=X1, out=open
  not not_3 (not_3_out, X0);
  and and_1 (and_1_out, not_1_out, not_3_out);
  and and_2 (and_2_out, X1, not_3_out);
  or or_1 (E, and_1_out, and_2_out);
endmodule

module F (
  input  X2,
  input  X1,
  input  X0,
  output F
);

  wire and_1_out, not_2_out, not_3_out;

  // NOT_Gate not_1 has open pins: in=X2, out=open
  not not_2 (not_2_out, X1);
  not not_3 (not_3_out, X0);
  and and_1 (and_1_out, not_2_out, not_3_out);
  or or_1 (F, X2, and_1_out);
endmodule

module G (
  input  X2,
  input  X1,
  input  X0,
  output G
);

  // NOT_Gate not_1 has open pins: in=X2, out=open
  // NOT_Gate not_2 has open pins: in=X1, out=open
  // NOT_Gate not_3 has open pins: in=X0, out=open
  or or_1 (G, X2, X1);
endmodule
