// Logisim project kodelaas_pdthorsr.circ as structural Verilog: 3 circuits, main circuit main
module main (
);

  wire _1_out, _2_out, _3_out, _4_out, _5_out, _6_out, _7_out, clock_1_out,
       kombinatoriskkretsholdkapabel_1_d0, kombinatoriskkretsholdkapabel_1_d1,
       kombinatoriskkretsholdkapabel_1_out, Q0_q, Q1_q;
  wire [2:0] priority_encoder_1_out;

  Button _1 (.out(_1_out));
  Button _4 (.out(_4_out));
  Button _2 (.out(_2_out));
  Button _5 (.out(_5_out));
  Button _7 (.out(_7_out));
  Button _3 (.out(_3_out));
  Button _6 (.out(_6_out));
  Priority_Encoder priority_encoder_1 (
    .in1(_1_out), .in2(_2_out), .in3(_3_out), .in4(_4_out), .in5(_5_out), .in6(_6_out), .in7(_7_out),
    .out(priority_encoder_1_out));  // open: in0, en_in, gs, en_out
  kombinatoriskKretsHoldKapabel kombinatoriskkretsholdkapabel_1 (
    .Q1(Q1_q), .Q0(Q0_q), .X2(priority_encoder_1_out[2]), .X1(priority_encoder_1_out[1]),
    .X0(priority_encoder_1_out[0]), .D1(kombinatoriskkretsholdkapabel_1_d1),
    .D0(kombinatoriskkretsholdkapabel_1_d0), .Out(kombinatoriskkretsholdkapabel_1_out));
  Clock clock_1 (.out(clock_1_out));
  D_Flip_Flop Q1 (.clk(clock_1_out), .D(kombinatoriskkretsholdkapabel_1_d1), .Q(Q1_q));  // open: Qn, preset, en, reset
  D_Flip_Flop Q0 (.clk(clock_1_out), .D(kombinatoriskkretsholdkapabel_1_d0), .Q(Q0_q));  // open: Qn, preset, en, reset
  LED led_1 (.in(kombinatoriskkretsholdkapabel_1_out));
endmodule

module kombinatoriskKrets (
  input  Q1,
  input  Q0,
  input  X2,
  input  X1,
  input  X0,
  output D1,
  output D0,
  output Out
);

  wire and_1_out, and_2_out, and_3_out, and_4_out, not_1_out, not_2_out, not_3_out, not_4_out, not_5_out,
       not_6_out, not_7_out, not_8_out, not_9_out, not_10_out, not_11_out, not_12_out, not_13_out,
       not_14_out, not_15_out;

  not not_1 (not_1_out, Q1);
  not not_2 (not_2_out, X2);
  not not_3 (not_3_out, Q0);
  not not_4 (not_4_out, X2);
  not not_5 (not_5_out, X0);
  not not_6 (not_6_out, Q1);
  not not_7 (not_7_out, Q0);
  not not_8 (not_8_out, X1);
  not not_9 (not_9_out, X0);
  not not_10 (not_10_out, Q0);
  not not_11 (not_11_out, X2);
  not not_12 (not_12_out, X0);
  not not_13 (not_13_out, Q0);
  not not_14 (not_14_out, X2);
  not not_15 (not_15_out, X0);
  and and_1 (and_1_out, not_1_out, Q0, not_2_out, X1, X0);
  and and_2 (and_2_out, Q1, not_3_out, not_4_out, X1, not_5_out);
  and and_3 (and_3_out, not_6_out, not_7_out, X2, not_8_out, not_9_out);
  and and_4 (and_4_out, Q1, not_10_out, not_11_out, X1, not_12_out);
  and and_5 (Out, Q1, not_13_out, not_14_out, X1, not_15_out);
  or or_1 (D1, and_1_out, and_2_out);
  or or_2 (D0, and_3_out, and_4_out);
endmodule

module kombinatoriskKretsHoldKapabel (
  input  Q1,
  input  Q0,
  input  X2,
  input  X1,
  input  X0,
  output D1,
  output D0,
  output Out
);

  wire and_1_out, and_2_out, and_3_out, and_4_out, not_1_out, not_2_out, not_3_out, not_4_out, not_5_out,
       not_6_out, not_7_out, not_8_out, not_9_out, not_10_out, not_11_out, not_12_out, not_13_out;

  not not_1 (not_1_out, Q1);
  not not_2 (not_2_out, X2);
  not not_3 (not_3_out, Q0);
  not not_4 (not_4_out, X2);
  not not_5 (not_5_out, Q1);
  not not_6 (not_6_out, X1);
  not not_7 (not_7_out, X0);
  not not_8 (not_8_out, Q0);
  not not_9 (not_9_out, X2);
  not not_10 (not_10_out, X0);
  not not_11 (not_11_out, Q0);
  not not_12 (not_12_out, X2);
  not not_13 (not_13_out, X0);
  and and_1 (and_1_out, not_1_out, Q0, not_2_out, X1, X0);
  and and_2 (and_2_out, Q1, not_3_out, not_4_out, X1);
  and and_3 (and_3_out, not_5_out, X2, not_6_out, not_7_out);
  and and_4 (and_4_out, Q1, not_8_out, not_9_out, X1, not_10_out);
  and and_5 (Out, Q1, not_11_out, not_12_out, X1, not_13_out);
  or or_1 (D1, and_1_out, and_2_out);
  or or_2 (D0, and_3_out, and_4_out);
endmodule
